// Logisim project sap1_1.circ as structural Verilog: 1 circuit, main circuit main
module main (
);

  wire A_sw1, A_sw2, A_sw3, A_sw4, and_1_out, C1_q1, C1_q2, C2_q1, C2_q2, C4_g4, C4_q1, C4_q2, C4_q3, C5_y1,
       C5_y2, C5_y3, C5_y4, C6_not_do1, C6_not_do2, C6_not_do3, C6_not_do4, C7_not_do1, C7_not_do2,
       C7_not_do3, C7_not_do4, C8_g4, C8_q1, C8_q2, C8_q3, CLK, CLR, Cp, dipswitch_1_sw1, dipswitch_1_sw2,
       dipswitch_1_sw3, dipswitch_1_sw4, dipswitch_1_sw5, dipswitch_1_sw6, dipswitch_1_sw7, dipswitch_1_sw8,
       Ep, NOT_CE, NOT_CLK, NOT_CLR, NOT_E1, NOT_L1, NOT_Lm, READ_WRITE_out, RUN_PROG_sw1, S2_sw1;

  DipSwitch dipswitch_1 (
    .sw1(dipswitch_1_sw1), .sw2(dipswitch_1_sw2), .sw3(dipswitch_1_sw3), .sw4(dipswitch_1_sw4),
    .sw5(dipswitch_1_sw5), .sw6(dipswitch_1_sw6), .sw7(dipswitch_1_sw7), .sw8(dipswitch_1_sw8));
  DipSwitch #(.number(1)) RUN_PROG (.sw1(RUN_PROG_sw1));
  DipSwitch #(.number(4)) A (.sw1(A_sw1), .sw2(A_sw2), .sw3(A_sw3), .sw4(A_sw4));
  and and_1 (and_1_out, NOT_CE, RUN_PROG_sw1);
  Button #(.press("passive")) READ_WRITE (.out(READ_WRITE_out));
  L_74LS107_f74dca52 C2 (
    .CLK1(NOT_CLK), .K1(Cp), .CLR1(NOT_CLR), .J2(Cp), .CLK2(C2_q1), .K2(Cp), .CLR2(NOT_CLR), .J1(Cp),
    .Q1(C2_q1), .Q2(C2_q2));  // open: NOTQ1, NOTQ2
  L_74LS107_f74dca52 C1 (
    .CLK1(C2_q2), .K1(Cp), .CLR1(NOT_CLR), .J2(Cp), .CLK2(C1_q1), .K2(Cp), .CLR2(NOT_CLR), .J1(Cp),
    .Q1(C1_q1), .Q2(C1_q2));  // open: NOTQ1, NOTQ2
  L_74LS173_6bdbcc89 C4 (
    .N(1'b0), .D1(C7_not_do1), .NOT_G1(NOT_Lm), .NOT_G2(NOT_Lm), .D2(C7_not_do2), .CLK(CLK), .D3(C7_not_do3),
    .D4(C7_not_do4), .CLR(1'b0), .M(1'b0), .Q1(C4_q1), .Q2(C4_q2), .Q3(C4_q3), .G4(C4_g4));
  L_74LS157_d074910b C5 (
    .B1(C4_g4), .A2(A_sw2), .B2(C4_q3), .A3(A_sw3), .B3(C4_q2), .A4(A_sw4), .B4(C4_q1), .STROBE_G(1'b0),
    .SELECT_A_B(S2_sw1), .A1(A_sw1), .Y1(C5_y1), .Y2(C5_y2), .Y3(C5_y3), .Y4(C5_y4));
  DipSwitch #(.number(1)) S2 (.sw1(S2_sw1));
  L_74LS189_c76b68cd C7 (
    .A0(C5_y4), .A1(C5_y3), .A2(C5_y2), .A3(C5_y1), .DI1(dipswitch_1_sw4), .DI2(dipswitch_1_sw3),
    .DI3(dipswitch_1_sw2), .DI4(dipswitch_1_sw1), .NOT_S(and_1_out), .NOT_W(READ_WRITE_out),
    .NOT_DO2(C7_not_do2), .NOT_DO3(C7_not_do3), .NOT_DO4(C7_not_do4), .NOT_DO1(C7_not_do1));
  L_74LS189_c76b68cd C6 (
    .A0(C5_y4), .A1(C5_y3), .A2(C5_y2), .A3(C5_y1), .DI1(dipswitch_1_sw8), .DI2(dipswitch_1_sw7),
    .DI3(dipswitch_1_sw6), .DI4(dipswitch_1_sw5), .NOT_S(and_1_out), .NOT_W(READ_WRITE_out),
    .NOT_DO2(C6_not_do2), .NOT_DO3(C6_not_do3), .NOT_DO4(C6_not_do4), .NOT_DO1(C6_not_do1));
  L_74LS173_6bdbcc89 C9 (
    .N(NOT_E1), .D1(C7_not_do1), .NOT_G1(NOT_L1), .NOT_G2(NOT_L1), .D2(C7_not_do2), .CLK(CLK),
    .D3(C7_not_do3), .D4(C7_not_do4), .CLR(1'b0), .M(NOT_E1), .Q1(C7_not_do1), .Q2(C7_not_do2),
    .Q3(C7_not_do3), .G4(C7_not_do4));
  L_74LS173_6bdbcc89 C8 (
    .N(1'b0), .D1(C6_not_do1), .NOT_G1(NOT_L1), .NOT_G2(NOT_L1), .D2(C6_not_do2), .CLK(CLK), .D3(C6_not_do3),
    .D4(C6_not_do4), .CLR(CLR), .M(1'b0), .Q1(C8_q1), .Q2(C8_q2), .Q3(C8_q3), .G4(C8_g4));
  L_74LS126_5b2bd483 C3 (
    .A1(C2_q1), .G1(Ep), .A2(C2_q2), .G2(Ep), .A3(C1_q1), .G3(Ep), .A4(C1_q2), .G4(Ep), .Y1(C7_not_do4),
    .Y2(C7_not_do3), .Y3(C7_not_do2), .Y4(C7_not_do1));

  // Notes on the sheet:
  //   S2
  //   Instruction Register
  //   RAM
  //   S4
  //   Program Counter
  //   MAR
  //   2 to 1 Multiplexer
endmodule
